// Logisim project HCount.circ as structural Verilog: 2 circuits, main circuit main
module main (
);

  wire and_1_out, and_2_out, and_3_out, and_4_out, and_5_out, and_6_out, and_7_out, and_8_out, and_9_out,
       and_10_out, and_11_out, and_12_out, and_13_out, and_14_out, and_15_out, and_16_out, and_18_out,
       and_19_out, clock_1_out, d_ff_1_q, d_ff_2_q, d_ff_3_q, d_ff_4_q, j_k_ff_4_q, j_k_ff_5_q, j_k_ff_5_qn,
       j_k_ff_6_q, n74138_1_pin11, n74138_1_pin12, n74138_1_pin15, n74153_1_pin6, n74153_1_pin10,
       n74153_2_pin6, n74153_2_pin10, n74157_1_pin1, n74157_1_pin15, n74157_2_pin15, n74161_1_pin1,
       n74161_1_pin3, n74161_1_pin11, n74161_1_pin14, n74161_2_pin1, n74161_2_pin3, n74161_2_pin4,
       n74161_2_pin5, n74161_2_pin6, n74161_2_pin7, n74161_2_pin9, n74161_3_pin1, n74161_3_pin3,
       n74161_3_pin4, n74161_3_pin5, n74161_3_pin6, n74161_3_pin7, n74161_4_pin1, n74161_4_pin2,
       n74161_4_pin3, n74161_4_pin4, n74161_4_pin5, n74161_4_pin6, n74161_4_pin7, n74161_4_pin9,
       n74161_4_pin15, n74161_5_pin1, n74161_5_pin3, n74161_5_pin4, n74161_5_pin5, n74161_5_pin6,
       n74161_5_pin7, n74166_1_pin1, n74166_1_pin2, n74166_1_pin3, n74166_1_pin4, n74166_1_pin5,
       n74166_1_pin6, n74166_1_pin7, n74166_1_pin9, n74166_1_pin10, n74166_1_pin11, n74166_1_pin12,
       n74166_1_pin13, n74166_1_pin14, n74273_1_pin1, n74273_1_pin2, n74273_1_pin5, n74273_1_pin6,
       n74273_1_pin9, n74273_1_pin11, n74273_1_pin12, n74273_1_pin15, n74273_1_pin16, n74273_1_pin19,
       n74273_2_pin1, not_4_out, not_5_out, not_6_out, not_7_out, not_8_out, not_9_out, not_10_out,
       not_11_out, not_13_out, not_14_out, not_15_out, not_16_out, not_17_out, not_18_out, not_24_out,
       not_25_out, not_26_out, or_1_out, or_2_out, or_3_out, or_4_out;
  wire [3:0] n74153_2_pin5, n74153_2_pin7, n74157_1_pin4, n74157_2_pin4, register_2_q;
  wire [7:0] multiplexer_1_out, multiplexer_3_out, n74273_1_pin3, n74273_2_pin3, register_1_q,
       rgb_video_1_p6, rom_2_data;
  wire [8:0] j_k_ff_2_q, n74161_1_pin13;

  // NOT_Gate not_1 is placed but not wired
  J_K_Flip_Flop j_k_ff_1 ();  // open: J, clk, K, Q, Qn, preset, reset
  Clock clock_1 (.out(clock_1_out));
  _74161 #(.ShowInternalStructure("true")) u_74161_1 (
    .pin1(n74161_1_pin1), .pin2(clock_1_out), .pin3(n74161_1_pin3), .pin4(n74161_1_pin3),
    .pin5(n74161_1_pin3), .pin6(n74161_1_pin3), .pin7(n74161_1_pin3), .pin14(n74161_1_pin14),
    .pin13(n74161_1_pin13[0]), .pin12(n74161_1_pin13[1]), .pin11(n74161_1_pin11), .pin10(n74161_1_pin3),
    .pin9(n74161_1_pin3));  // open: pin15
  _74161 #(.ShowInternalStructure("true")) u_74161_2 (
    .pin1(n74161_2_pin1), .pin2(n74161_1_pin11), .pin3(n74161_2_pin3), .pin4(n74161_2_pin4),
    .pin5(n74161_2_pin5), .pin6(n74161_2_pin6), .pin7(n74161_2_pin7), .pin14(n74161_1_pin13[7]),
    .pin13(n74161_1_pin13[8]), .pin10(n74161_2_pin7), .pin9(n74161_2_pin9));  // open: pin15, pin12, pin11
  _74161 #(.ShowInternalStructure("true")) u_74161_3 (
    .pin1(n74161_3_pin1), .pin2(n74161_1_pin11), .pin3(n74161_3_pin3), .pin4(n74161_3_pin4),
    .pin5(n74161_3_pin5), .pin6(n74161_3_pin6), .pin7(n74161_3_pin7), .pin15(n74161_2_pin7),
    .pin14(n74161_1_pin13[3]), .pin13(n74161_1_pin13[4]), .pin12(n74161_1_pin13[5]),
    .pin11(n74161_1_pin13[6]), .pin10(n74161_3_pin7), .pin9(n74161_2_pin9));
  _74161 #(.ShowInternalStructure("true")) u_74161_4 (
    .pin1(n74161_4_pin1), .pin2(n74161_4_pin2), .pin3(n74161_4_pin3), .pin4(n74161_4_pin4),
    .pin5(n74161_4_pin5), .pin6(n74161_4_pin6), .pin7(n74161_4_pin7), .pin15(n74161_4_pin15),
    .pin14(j_k_ff_2_q[4]), .pin13(j_k_ff_2_q[5]), .pin12(j_k_ff_2_q[6]), .pin11(j_k_ff_2_q[7]),
    .pin10(n74161_4_pin7), .pin9(n74161_4_pin9));
  _74161 #(.ShowInternalStructure("true")) u_74161_5 (
    .pin1(n74161_5_pin1), .pin2(n74161_4_pin2), .pin3(n74161_5_pin3), .pin4(n74161_5_pin4),
    .pin5(n74161_5_pin5), .pin6(n74161_5_pin6), .pin7(n74161_5_pin7), .pin15(n74161_4_pin7),
    .pin14(j_k_ff_2_q[0]), .pin13(j_k_ff_2_q[1]), .pin12(j_k_ff_2_q[2]), .pin11(j_k_ff_2_q[3]),
    .pin10(n74161_5_pin7), .pin9(n74161_4_pin9));
  J_K_Flip_Flop j_k_ff_2 (
    .J(n74161_4_pin15), .clk(n74161_4_pin2), .K(and_3_out), .Q(j_k_ff_2_q[8]));  // open: Qn, preset, reset
  and and_1 (and_1_out, n74161_1_pin11, n74161_1_pin13[1], n74161_1_pin13[0], n74161_1_pin14);
  and and_2 (and_2_out, n74161_1_pin13[7], n74161_1_pin13[8], n74161_1_pin13[6]);
  not not_2 (n74161_2_pin9, and_2_out);
  and and_3 (and_3_out, j_k_ff_2_q[8], and_4_out);
  not not_3 (n74161_4_pin9, and_3_out);
  not not_4 (not_4_out, n74161_1_pin13[7]);
  not not_5 (not_5_out, j_k_ff_2_q[7]);
  and and_4 (and_4_out, j_k_ff_2_q[2], j_k_ff_2_q[0]);
  and and_5 (and_5_out, n74161_1_pin13[8], not_4_out, n74161_1_pin13[6]);
  D_Flip_Flop d_ff_1 (.clk(n74161_4_pin2), .D(and_3_out), .Q(d_ff_1_q));  // open: Qn, preset, reset
  and and_6 (and_6_out, n74161_1_pin13[3], n74161_1_pin13[7], n74161_1_pin13[8]);
  _74138 #(.ShowInternalStructure("true")) u_74138_1 (
    .pin1(j_k_ff_2_q[3]), .pin2(j_k_ff_2_q[4]), .pin3(j_k_ff_2_q[5]), .pin4(j_k_ff_2_q[8]), .pin5(not_5_out),
    .pin6(j_k_ff_2_q[6]), .pin15(n74138_1_pin15), .pin12(n74138_1_pin12), .pin11(n74138_1_pin11));  // open: pin7, pin14, pin13, pin10, pin9
  not not_6 (not_6_out, and_7_out);
  and and_7 (and_7_out, and_5_out, n74161_1_pin13[5], n74161_1_pin13[4]);
  and and_8 (and_8_out, and_5_out, j_k_ff_5_qn, n74161_2_pin7);
  not not_7 (not_7_out, n74138_1_pin12);
  not not_8 (not_8_out, n74138_1_pin11);
  not not_9 (not_9_out, n74138_1_pin15);
  and and_9 (and_9_out, and_5_out, not_6_out, n74161_1_pin13[4]);
  not not_10 (not_10_out, n74161_1_pin13[8]);
  // Probe on not_10_out
  and and_10 (and_10_out, not_7_out, and_4_out);
  not not_11 (not_11_out, n74161_1_pin11);
  J_K_Flip_Flop #(.trigger("falling")) j_k_ff_3 (
    .J(and_9_out), .clk(not_11_out), .K(and_7_out), .Q(n74161_4_pin2));  // open: Qn, preset, reset
  D_Flip_Flop d_ff_2 (.clk(n74161_1_pin11), .D(not_10_out), .Q(d_ff_2_q));  // open: Qn, preset, reset
  J_K_Flip_Flop #(.trigger("falling")) j_k_ff_4 (
    .J(and_8_out), .clk(not_11_out), .K(and_6_out), .Q(j_k_ff_4_q));  // open: Qn, preset, reset
  J_K_Flip_Flop #(.trigger("falling")) j_k_ff_5 (
    .J(and_10_out), .clk(not_11_out), .K(not_8_out), .Q(j_k_ff_5_q), .Qn(j_k_ff_5_qn));  // open: preset, reset
  J_K_Flip_Flop #(.trigger("falling")) j_k_ff_6 (
    .J(d_ff_1_q), .clk(not_11_out), .K(not_9_out), .Q(j_k_ff_6_q));  // open: Qn, preset, reset
  not not_12 (n74161_1_pin13[2], n74161_1_pin11);
  and and_11 (and_11_out, d_ff_2_q, j_k_ff_6_q);
  // Probe on n74161_1_pin13
  or or_1 (or_1_out, and_12_out, and_13_out);
  // RGB_Video #(.cursor("No Cursor"), .height(262), .scale(1), .width(458)) rgb_video_1: pin names not known; wires that end beside it: 1'b0, n74161_1_pin14, 1'b1, n74161_1_pin13, j_k_ff_2_q, rgb_video_1_p6
  // Probe on j_k_ff_2_q
  and and_12 (and_12_out, n74161_1_pin13[0], 1'b0);
  and and_13 (and_13_out, n74161_1_pin14, not_13_out);
  Multiplexer #(.width(8)) multiplexer_1 (.in0(register_1_q), .in1(8'hb), .out(multiplexer_1_out), .sel(j_k_ff_4_q));
  not not_13 (not_13_out, 1'b0);
  Multiplexer #(.width(8)) multiplexer_2 (.in0(multiplexer_3_out), .in1(8'hc), .out(rgb_video_1_p6), .sel(j_k_ff_5_q));
  Multiplexer #(.width(8)) multiplexer_3 (
    .in0(multiplexer_1_out), .in1(8'hd), .out(multiplexer_3_out), .sel(n74161_4_pin2));
  Register register_1 (.D({4'b0000, n74153_2_pin7}), .en(1'b1), .Q(register_1_q), .clk(or_1_out));  // open: clr
  // Probe on j_k_ff_5_q
  or or_2 (or_2_out, not_10_out, and_11_out);
  _74273 #(.ShowInternalStructure("true")) u_74273_1 (
    .pin1(n74273_1_pin1), .pin2(n74273_1_pin2), .pin3(n74273_1_pin3[0]), .pin4(n74273_1_pin3[1]),
    .pin5(n74273_1_pin5), .pin6(n74273_1_pin6), .pin7(n74273_1_pin3[2]), .pin8(n74273_1_pin3[3]),
    .pin9(n74273_1_pin9), .pin19(n74273_1_pin19), .pin18(n74273_1_pin3[7]), .pin17(n74273_1_pin3[6]),
    .pin16(n74273_1_pin16), .pin15(n74273_1_pin15), .pin14(n74273_1_pin3[5]), .pin13(n74273_1_pin3[4]),
    .pin12(n74273_1_pin12), .pin11(n74273_1_pin11));
  not not_14 (not_14_out, and_1_out);
  not not_15 (not_15_out, not_14_out);
  and and_14 (and_14_out, not_15_out, not_18_out);
  not not_16 (not_16_out, and_14_out);
  D_Flip_Flop d_ff_3 (.clk(n74166_1_pin7), .D(n74166_1_pin13), .Q(d_ff_3_q), .reset(not_13_out));  // open: Qn, preset
  not not_17 (not_17_out, and_11_out);
  _74166 #(.ShowInternalStructure("true")) u_74166_1 (
    .pin1(n74166_1_pin1), .pin2(n74166_1_pin2), .pin3(n74166_1_pin3), .pin4(n74166_1_pin4),
    .pin5(n74166_1_pin5), .pin6(n74166_1_pin6), .pin7(n74166_1_pin7), .pin15(not_16_out),
    .pin14(n74166_1_pin14), .pin13(n74166_1_pin13), .pin12(n74166_1_pin12), .pin11(n74166_1_pin11),
    .pin10(n74166_1_pin10), .pin9(n74166_1_pin9));
  _74153 #(.ShowInternalStructure("true")) u_74153_1 (
    .pin1(not_17_out), .pin2(d_ff_3_q), .pin3(n74273_1_pin16), .pin4(n74273_1_pin6), .pin5(n74153_2_pin5[2]),
    .pin6(n74153_1_pin6), .pin7(n74153_2_pin7[2]), .pin15(not_17_out), .pin14(n74166_1_pin13),
    .pin13(n74273_1_pin19), .pin12(n74273_1_pin9), .pin11(n74153_2_pin5[3]), .pin10(n74153_1_pin10),
    .pin9(n74153_2_pin7[3]));
  _74157 #(.ShowInternalStructure("true")) u_74157_1 (
    .pin1(n74157_1_pin1), .pin2(n74273_1_pin3[0]), .pin3(n74166_1_pin14), .pin4(n74157_1_pin4[0]),
    .pin5(n74273_1_pin3[1]), .pin6(n74166_1_pin12), .pin7(n74157_1_pin4[1]), .pin15(n74157_1_pin15),
    .pin14(n74273_1_pin3[2]), .pin13(n74166_1_pin10), .pin12(n74157_1_pin4[3]), .pin11(n74273_1_pin3[3]),
    .pin10(n74166_1_pin11), .pin9(n74157_1_pin4[2]));
  not not_18 (not_18_out, n74157_1_pin1);
  not not_19 (n74166_1_pin7, n74161_1_pin14);
  D_Flip_Flop d_ff_4 (.clk(n74166_1_pin7), .D(not_15_out), .Q(d_ff_4_q));  // open: Qn, preset, reset
  Register #(.width(4)) register_2 (.D(n74157_1_pin4), .en(1'b1), .Q(register_2_q), .clk(or_3_out), .clr(and_15_out));
  or or_3 (or_3_out, and_19_out, 1'b0);
  _74153 #(.ShowInternalStructure("true")) u_74153_2 (
    .pin1(not_17_out), .pin2(d_ff_3_q), .pin3(n74273_1_pin12), .pin4(n74273_1_pin2), .pin5(n74153_2_pin5[0]),
    .pin6(n74153_2_pin6), .pin7(n74153_2_pin7[0]), .pin15(not_17_out), .pin14(n74166_1_pin13),
    .pin13(n74273_1_pin15), .pin12(n74273_1_pin5), .pin11(n74153_2_pin5[1]), .pin10(n74153_2_pin10),
    .pin9(n74153_2_pin7[1]));
  not not_20 (n74153_1_pin10, register_2_q[3]);
  not not_21 (n74153_1_pin6, register_2_q[2]);
  not not_22 (n74153_2_pin10, register_2_q[1]);
  not not_23 (n74153_2_pin6, register_2_q[0]);
  _74157 #(.ShowInternalStructure("true")) u_74157_2 (
    .pin1(n74157_1_pin1), .pin2(n74273_1_pin3[4]), .pin3(n74166_1_pin14), .pin4(n74157_2_pin4[0]),
    .pin5(n74273_1_pin3[5]), .pin6(n74166_1_pin12), .pin7(n74157_2_pin4[1]), .pin15(n74157_2_pin15),
    .pin14(n74273_1_pin3[7]), .pin13(n74166_1_pin10), .pin12(n74157_2_pin4[3]), .pin11(n74273_1_pin3[6]),
    .pin10(n74166_1_pin11), .pin9(n74157_2_pin4[2]));
  not not_24 (not_24_out, or_2_out);
  Register #(.width(4)) register_3 (.D(n74157_2_pin4), .en(1'b1), .Q(n74153_2_pin5), .clk(or_4_out), .clr(and_15_out));
  or or_4 (or_4_out, and_18_out, 1'b0);
  and and_15 (and_15_out, not_24_out, 1'b1);
  not not_25 (not_25_out, n74166_1_pin4);
  and and_16 (and_16_out, n74166_1_pin2, n74166_1_pin3, not_25_out);
  and and_17 (n74157_1_pin1, 1'b1, and_16_out);
  and and_18 (and_18_out, n74157_1_pin1, n74166_1_pin5, d_ff_4_q);
  and and_19 (and_19_out, n74157_1_pin1, not_26_out, d_ff_4_q);
  _74273 #(.ShowInternalStructure("true")) u_74273_2 (
    .pin1(n74273_2_pin1), .pin2(n74166_1_pin14), .pin3(n74273_2_pin3[0]), .pin4(n74273_2_pin3[1]),
    .pin5(n74166_1_pin12), .pin6(n74166_1_pin11), .pin7(n74273_2_pin3[2]), .pin8(n74273_2_pin3[3]),
    .pin9(n74166_1_pin10), .pin19(n74166_1_pin2), .pin18(n74273_2_pin3[7]), .pin17(n74273_2_pin3[6]),
    .pin16(n74166_1_pin3), .pin15(n74166_1_pin4), .pin14(n74273_2_pin3[5]), .pin13(n74273_2_pin3[4]),
    .pin12(n74166_1_pin5), .pin11(not_11_out));
  not not_26 (not_26_out, n74166_1_pin5);
  // Probe on j_k_ff_2_q
  ROM #(.addrWidth(11)) rom_1 (.addr({rom_2_data, j_k_ff_2_q[2:0]}), .data(n74273_2_pin3));
  ROM #(.addrWidth(12)) rom_2 (.addr({2'b00, j_k_ff_2_q[7:3], n74161_1_pin13[7:3]}), .data(rom_2_data));
  // Probe on {2'b00, j_k_ff_2_q[7:3], n74161_1_pin13[7:3]}
  _74157 #(.ShowInternalStructure("true")) u_74157_3 ();  // open: pin1, pin2, pin3, pin4, pin5, pin6, pin7, pin15, pin14, pin13, pin12, pin11, pin10, pin9
  _74157 #(.ShowInternalStructure("true")) u_74157_4 ();  // open: pin1, pin2, pin3, pin4, pin5, pin6, pin7, pin15, pin14, pin13, pin12, pin11, pin10, pin9
  // also tied to GND on the sheet: {n74161_2_pin3, n74161_2_pin4, n74161_2_pin5, n74161_2_pin6, n74161_3_pin3, n74161_3_pin4, n74161_3_pin5, n74161_3_pin6, n74161_4_pin3, n74161_4_pin4, n74161_4_pin5, n74161_4_pin6, n74161_5_pin3, n74161_5_pin4, n74161_5_pin5, n74161_5_pin6, n74273_1_pin11, n74166_1_pin6, n74166_1_pin1, n74157_1_pin15, n74157_2_pin15}
  // also tied to VCC on the sheet: {n74161_1_pin1, n74161_2_pin1, n74161_3_pin1, n74161_3_pin7, n74161_4_pin1, n74161_5_pin1, n74161_5_pin7, n74161_1_pin3, n74273_1_pin1, n74166_1_pin9, n74273_2_pin1}

  // Notes on the sheet:
  //   U30 Dual DFF
  //   U31 Dual JK
  //   U32 Tripe 3-AND
  //   U33 Dual JK
  //   U34 Quad 2-AND
  //   U35 4-bit Counter
  //   U36 4-bit Counter
  //   U37 Tripe 3-AND
  //   U38 Hex Inverter
  //   U39 8-bit Shift Register
  //   U40 4-bit Counter
  //   U41 4-bit Counter
  //   U42 1 of 8 Decoder
  //   U43 Dual JK (1/2)
  //   U44 Hex Inverter (5/6)
  //   U44F
  //   U43B
  //   CLK
  //   14.31818 MHz
  //   MUST update Address on /CLK mid-cycle
  //   Address setup for mid-high-CLK RAS
  //   13 Chips H & V
  //   6-bit H-Count
  //   [0-56]
  //   U35
  //   U36
  //   9-bit V-Count
  //   U43A
  //   U40
  //   U41
  //   VScan= ~(d8+(d7•d6))
  //   U38A
  //   VBlank = 76~543 + 765~4~3 + 765~4~2
  //   VSync = VBL • ~(d4 + d3 + d2) • (d1 + d0)
  //   N/A
  //   7.15909 MHz
  //   3.579545 MHz
  //   1.7897725 MHz
  //   0.894886 MHz
  //   RHC 56
  //   111xxx
  //   U32A
  //   RVC 261
  //   (100 000 101)
  //   RVC
  //   U34B
  //   U38F
  //   1x1
  //   U34A
  //   Work-around for incorrectly timed RCO output
  //   1 in 16
  //   U38B
  //   U44A
  //   U30B
  //   Line Delay
  //   SHB 40
  //   101xxx
  //   U32B
  //   011
  //   Not VSync
  //   RCB 49
  //   11xxx1
  //   U32C
  //   VSync
  //   Not HBlank
  //   U42
  //   HBlank
  //   RHS 46
  //   10111x
  //   U37B
  //   SCB 47
  //   101111
  //   U37C
  //   000
  //   011
  //   100
  //   Colorburst
  //   Not Burst
  //   VBlank
  //   Not VBlank
  //   Negate Negative Edge (74LS73)
  //   Must be rising-edge for 8px delay
  //   U38C
  //   Fetch
  //   U44B
  //   U44C
  //   U44D
  //   HSync
  //   Not HSync
  //   Scan
  //   NotScan
  //   SHS 42
  //   101x1x
  //   U37A
  //   U38D
  //   U31B
  //   Colorburst
  //   U34C
  //   U44E
  //   U31A
  //   HSync
  //   U30A
  //   Visible
  //   U33A
  //   VSync
  //   U33B
  //   Visible
  //   HBlank
  //   Not HBlank
  //   --
  //   --
  //   VBlank
  //   Not VBlank
  //   7.15909 MHz
  //   N/A
  //   Scanout
  //   U34D
  //   VSync
  //   Not VSync
  //   VSync
  //   Not VSync
  //   HSync
  //   Not HSync
  //   Scan
  //   NotScan
  //   HCount
  //   VCount
  //   HSync
  //   Burst
  //   Scanout
  //   DAC Latch
  //   74LS175
  //   VSync
  //   VSync
  //   VDP_2BPP
  //   Most home computers/consoles
  //   use 0 IRE for both Black and Blanking level
  //   (that would eliminate HBlank and VBlank)
  //   Fetch
  //   Last high PCLK in the CLK cycle
  //   Scanout
  //   U52
  //   COL2/3
  //   U38E
  //   nLoad
  //   Delay beyond \PCLK edge
  //   U45A
  //   MUST load on \PCLK aligned with \CLK
  //   U39
  //   U50
  //   FG
  //   MUX
  //   IOQ_FE
  //   Shift Register
  //   \PCLK
  //   \PCLK
  //   U46
  //   U46
  //   Col MUX 2,3
  //   U45B
  //   ~Q outputs
  //   U48
  //   FG
  //   MUX
  //   Fetch
  //   Inhibit Load of Cx/Dx in Text mode
  //   U51
  //   BG
  //   LoadQ on \PCLK aligned with \CLK
  //   U47
  //   U47
  //   Col MUX 0,1
  //   Hold FG/BG in Reset until Fetch begins
  //   Q outputs
  //   U49
  //   BG
  //   Data Bus
  //   IOQ_FD
  //   VDP_TEXT
  //   U53
  //   Cx/Dx decode
  //   Cx/Dx Text
  //   LoadQ
  //   Holding Latch
  //   MUST latch at /CLK mid-cycle for VDP
  //   Bus CLK 0.89 MHz
  //   V[0..2]
  //   H[3..8]
  //   Shift Reg
  //   V[3..8]
  //   Char
  //   line
  //   contents of rom_1 (hex, n*v repeats v):
  //   cc 33 cc 33 cc 33 cc 33 1 85 b5 fd b5 85 1 0 1 85 31 fd 31 1 85 0 30 fc fd fd b5 85 1 0 1 85 b5 fd
  //   b4 1 85 4*0 ab ab 81 81 81 0 0 0 d5 d5 6*81 ab ab 0 0 0 81 81 81 d5 d5 6*0 ff ff 0 0 0 11*81 ff ff
  //   6*0 ff ff 6*81 ab ab 6*81 d5 d5 6*81 ff ff 81 81 81 a 28 a0 81 5 14 50 40 50 14 5 81 a0 28 a 2 5a 3c
  //   a4 81 25 3c 5a 42 0 0 81 a5 a5 81 4*0 81 24 24 81 5*0 a9 a9 81 81 4*0 95 95 81 81 0 0 81 81 a9 a9
  //   4*0 81 81 95 95 6*0 bd bd 4*0 6*81 0 0 81 81 bd bd 6*0 bd bd 81 81 0 0 81 81 a9 a9 81 81 0 0 81 81
  //   95 95 81 81 0 0 81 81 bd bd 81 81 9*0 4*81 0 81 81 0 2d 2d 2d 5*0 2d 2d bf 2d bf 2d 2d 0 80 ad 94 ad
  //   8a ad 80 0 6 19 24 80 9 26 18 0 5 90 94 5 9b b0 2d 0 81 81 5 5*0 81 5 14 14 14 5 81 0 a0 28 a a a 28
  //   a0 0 0 2d a1 bf a1 2d 0 0 0 a0 a0 af a0 a0 7*0 81 81 5 0 0 0 af 9*0 81 81 0 2 a 28 a0 81 5 14 0 a5
  //   3c bc 3d 3c 3c a5 0 81 85 95 81 81 81 bd 0 a5 3c 28 a0 81 5 bd 0 a5 3c 28 a1 28 3c a5 0 a0 a1 a4 b4
  //   bd a0 a0 0 bd 14 b5 28 28 3c a5 0 a5 3c 14 b5 3c 3c a5 0 bd 28 a0 81 5 14 14 0 a5 3c 3c a5 3c 3c a5
  //   0 a5 3c 3c ad 28 3c a5 0 0 0 a0 a0 0 a0 a0 0 0 0 a0 a0 0 a0 a0 81 28 a0 81 5 81 a0 28 0 0 0 ad 0 ad
  //   0 0 0 5 81 a0 28 a0 81 5 0 a5 3c 28 a0 0 81 81 0 a9 6 b2 33 98 4 a9 0 a5 3c 3c bd 3c 3c 3c 0 b5 3c
  //   3c b5 3c 3c b5 0 a5 3c 14 14 14 3c a5 0 95 b4 3c 3c 3c b4 95 0 bd 14 14 b5 14 14 bd 0 bd 14 14 b5 14
  //   14 14 0 a5 3c 14 bc 3c 3c a5 0 3c 3c 3c bd 3c 3c 3c 0 bd 5*81 bd 0 ad 4*a0 b4 85 0 3c b4 95 15 95 b4
  //   3c 0 6*14 bd 0 1e 3f bf 9e 1e 1e 1e 0 3c 3c 3d bd bc 3c 3c 0 a5 5*3c a5 0 b5 3c 3c b5 14 14 14 0 a5
  //   3c 3c 3c 9c b4 2d 0 b5 3c 3c b5 b4 3c 3c 0 a5 3c 14 a5 28 3c a5 0 bd 6*81 0 6*3c a5 0 5*3c a5 81 0
  //   1e 1e 1e 9e bf 3f 1e 0 3c 3c a5 81 a5 3c 3c 0 3c 3c 3c a5 81 81 81 0 bd 28 a0 81 5 14 bd 0 b5 5*14
  //   b5 0 14 5 81 a0 28 a 2 0 ad 5*28 ad 0 81 a5 3c 12*0 bf 14 5 81 7*0 a5 28 ad 3c a5 0 14 14 b5 3c 3c
  //   3c b5 0 0 0 a5 3c 14 3c a5 0 28 28 ad 3c 3c 3c ad 0 0 0 a5 3c b5 14 a5 0 a9 5 5 b5 5 5 5 0 0 0 a5 3c
  //   3c ad 28 b5 14 14 14 b5 3c 3c 3c 0 0 81 0 85 81 81 a5 0 0 a0 0 a1 a0 a0 b4 85 14 14 3c b4 95 b4 3c 0
  //   85 5*81 a5 0 0 0 2d bf 9e 9e 1e 0 0 0 b5 4*3c 0 0 0 a5 3c 3c 3c a5 0 0 0 b5 3c 3c 3c b5 14 0 0 ad 3c
  //   3c 3c ad 28 0 0 b5 3c 14 14 14 0 0 0 a5 14 a5 28 a5 0 0 5 b5 5 5 2d a1 0 0 0 4*3c a5 0 0 0 3c 3c 3c
  //   a5 81 0 0 0 1e 9e 9e bf 2d 0 0 0 3c a5 81 a5 3c 0 0 0 3c 3c 3c ad 28 a5 0 0 bd a0 81 5 bd 0 28 a0 a0
  //   81 a0 a0 28 0 7*81 0 5 81 81 a0 81 81 5 0 0 0 7 9e 38 0 0 0 8*ff f 3c f0 c3 f 3c f0 c3 f 3c f0 42 a
  //   3c f0 c3 ff ff f0 c3 f 3c f0 c3 f 3c f0 c3 f 3c ff ff f 3e fa cb f 3e fa cb 5f 7c f0 d3 5f 7c f0 d3
  //   ff ff 12*0 ff ff 8*a 8*50 2 a 28 a0 81 5 14 50 40 50 14 5 81 a0 28 a 50 14 5 81 a0 28 a 2 a 28 a0 81
  //   5 14 50 40 50 14 5 81 81 5 14 50 ff ff 7*50 40 6*0 a 2 12*0 40 50 6*0 2 a 616*0 14 41 41 55 41 41 41
  //   0 54 41 41 54 41 41 54 0 14 41 40 40 40 41 14 0 50 44 41 41 41 44 50 0 55 40 40 54 40 40 55 0 55 40
  //   40 54 40 40 40 0 14 41 40 45 41 41 14 0 41 41 41 55 41 41 41 0 54 5*10 54 0 55 4*4 44 10 0 41 41 44
  //   50 44 41 41 0 6*40 55 0 41 55 5*41 0 41 51 55 45 41 41 41 0 14 5*41 14 0 54 41 41 54 40 40 40 0 14
  //   4*41 44 11 0 54 41 41 54 50 44 41 0 14 41 40 14 1 41 14 0 55 6*10 0 6*41 14 0 4*41 45 14 10 0 5*41
  //   55 41 0 41 41 41 14 41 41 41 0 41 41 41 14 10 10 10 0 55 1 4 4 10 40 55
  //   contents of rom_2 (hex, n*v repeats v):
  //   78 d8 a2 ff 9a a2 1 86 d9 ca 20 ec fe a0 23 20 9e fd a9 10 85 dc a9 5 85 75 85 77 a2 0 86 76 86 cc
  //   86 cd 86 cf 38 a5 dc e5 75 85 ce 20 e9 fa a0 3c 20 9e fd d8 20 ca ff a0 49 20 9e fd a2 ff 9a 20 85
  //   fe 84 c9 20 d2 fd a0 0 20 ef f0 c9 0 f0 ec 20 37 fa d0 2a a2 f3 a9 0 20 d7 f4 90 13 20 66 f0 4c 3e
  //   f0 29 7 a aa bd 35 f6 48 bd 34 f6 48 60 20 c2 f0 a9 1 85 7d a0 0 84 7c 4c 29 f7 a5 cf 85 78 a5 ce 85
  //   79 30 6 20 c2 f0 4c 3e f0 a0 e5 20 a4 fd a0 e9 20 9e fd 4c 3e f0 48 a0 c2 20 a4 fd 68 20 e5 fd 20 d2
  //   fd 4c 3e f0 a0 f7 20 9e fd a5 d2 30 fc 4c 3e f0 a0 ca 4c 93 f0 4c 4f f1 88 c8 20 ef f0 20 f9 f0 b0
  //   ee aa bd 0 f4 a2 f4 20 d7 f4 90 e8 9 c0 20 f2 f5 29 31 aa bd 1 f6 85 c8 29 f aa a9 f1 48 bd 21 f6 48
  //   60 b9 0 1 c8 c9 20 f0 f8 88 60 b9 0 1 29 df 38 e9 41 c9 1a 60 60 a5 c8 4*6a 29 7 85 c8 d0 3 20 e8 f1
  //   20 35 f2 c6 c8 d0 f6 60 20 5 f1 20 35 f2 90 6 20 35 f2 90 1 60 a9 0 4c f2 f5 20 e0 f1 20 f2 f5 85 c6
  //   b1 c4 c8 20 f2 f5 c6 c6 d0 f6 60 4c 5 f2 20 5 f2 20 e8 f1 20 35 f2 60 20 35 f2 85 c9 a9 3d 20 ea f1
  //   20 35 f2 c5 c9 d0 1 60 a0 e1 4c 93 f0 20 35 f2 a9 28 20 ea f1 20 35 f2 a9 29 20 ea f1 60 20 35 f2 29
  //   1 d0 e3 a9 3d 20 ea f1 20 35 f2 a2 f5 20 1d f2 90 41 20 35 f2 a2 f5 20 1d f2 90 93 4c 35 f2 20 ef f0
  //   20 f9 f0 b0 88 4c 35 f2 20 35 f2 a2 f5 20 1d f2 90 1f 90 5 20 34 f2 90 0 60 20 ee f5 86 c8 20 35 f2
  //   e6 c8 20 f8 f1 f0 f6 88 a5 c8 a2 0 95 c2 60 84 c9 a0 ca 20 a4 fd a4 c9 20 ad f6 20 d2 fd 4c 3e f0 86
  //   c6 a5 c9 18 e5 c6 60 a9 2c 85 ca 20 ef f0 c5 ca d0 2 c8 60 4c 9e f0 a9 2c 85 ca 20 ef f0 c5 ca d0 1
  //   c8 60 a9 23 20 ea f1 20 37 fa a5 ce d0 9 a5 cf c9 4 b0 3 4c f2 f5 4c 81 f9 20 ef f0 84 ca ca 88 e8
  //   c8 bd 0 f5 d1 c0 f0 f7 c9 80 b0 2 a4 ca 60 60 203*0 4c 49 53 54 c0 52 55 4e c1 41 52 54 c2 53 41 56
  //   45 c3 41 55 54 4f c4 44 45 4c c5 4e 45 57 c6 4f 4c 44 87 18 92 93 94 95 96 90 d d 50 69 78 69 65 20
  //   42 41 53 49 43 20 31 2e 30 d c 20 62 79 74 65 73 20 66 72 65 65 d 5 52 45 41 44 59 9 53 65 61 72 63
  //   68 69 6e 67 7 4c 6f 61 64 69 6e 67 3b 50 69 78 69 65 20 41 52 54 20 1c 1d 1e 1f 20 74 6f 20 6d 6f 76
  //   65 2c 20 47 52 41 2b 6b 65 79 20 74 6f 20 64 72 61 77 2c 20 43 4f 4c 2b 6b 65 79 20 66 6f 72 20 63
  //   6f 6c 6f 72 12 50 72 65 73 73 20 50 4c 41 59 20 6f 6e 20 54 41 50 45 12 50 72 65 73 73 20 53 54 4f
  //   50 20 6f 6e 20 54 41 50 45 7 45 78 70 65 63 74 20 6 53 79 6e 74 61 78 3 44 49 56 3 4f 56 46 3 50 52
  //   47 3 56 41 52 3 54 59 50 3 52 4e 47 7 20 45 72 72 6f 72 d 5 42 6c 6f 63 6b 6 45 73 63 61 70 65 0 0
  //   1a 1a 1a 24 31 3a 3e 49 49 52 52 52 60 65 6a 73 87 87 a6 ac ac b2 b2 b7 b7 b7 43 4c 53 81 43 4c 4f
  //   53 45 c2 44 41 54 41 83 44 49 4d 84 44 45 46 c5 45 4c 53 45 86 45 4e 44 c7 46 4f 52 c8 47 4f 54 4f
  //   89 47 4f 53 55 42 ca 49 46 8b 49 4e 50 55 54 cc 4c 45 54 8d 4c 49 4e 45 8e 4c 4f 41 44 cf 4d 4f 44
  //   45 d0 4e 45 58 54 d1 4f 50 54 92 4f 50 45 4e d3 50 55 54 94 50 52 49 4e 54 95 50 4c 4f 54 96 50 4f
  //   4b 45 d7 52 45 41 44 98 52 45 50 45 41 54 99 52 45 53 54 4f 52 45 9a 52 45 54 55 52 4e 9b 52 45 4d
  //   dc 53 4f 55 4e 44 dd 55 4e 54 49 4c de 57 41 49 54 df 0 1a 1e 24 29 2d 31 36 3a 3e 43 49 4c 52 56 5b
  //   60 65 6a 6e 73 77 7d 82 87 8c 93 9b a2 a6 ac b2 84 c6 85 c0 86 c1 a2 0 88 c8 e6 c0 a1 c0 d9 0 1 f0
  //   f6 10 2 38 60 e6 c0 a1 c0 10 fa e6 c0 a4 c6 a 10 e4 18 60 0 0 0 1a 22 26 2b 2b 2f 32 36 36 41 45 49
  //   53 58 58 58 5f 5f 6a 83 8c 90 4*99 41 42 53 c0 41 53 43 81 42 54 4e 82 43 48 52 24 83 45 4f 46 84 46
  //   4e 85 47 45 54 86 49 4e 53 54 52 24 c7 49 4e 54 88 4a 4f 59 89 4b 45 59 8a 4c 45 4e cb 4c 45 46 54
  //   24 8c 4d 49 44 24 8d 50 4f 53 ce 50 49 8f 52 49 47 48 54 24 d0 52 4e 44 91 53 43 4e d2 53 54 52 49
  //   4e 47 24 d3 53 54 52 24 d4 53 51 52 d5 53 47 4e 96 54 49 4d 45 d7 54 4f 50 98 55 53 52 99 56 41 4c
  //   da 56 50 4f 53 9b 0 4e 4f 54 ad 41 4e 44 bd 44 49 56 b3 45 4f 52 bf 4d 4f 44 b4 4f 52 be 41 54 ff 54
  //   4f ff 53 54 45 50 ff 54 48 45 4e ff 53 50 43 83 54 41 42 84 46 4e 0 1a 1e 22 26 2b 2f 32 36 3d 41 45
  //   49 4d 53 58 5c 5f 66 6a 6e 76 7b 7f 83 88 8c 90 94 9a 9e a2 a6 aa ae a5 7e 85 c2 a6 7e 9d 0 1 e6 7e
  //   30 1 60 a0 d5 4c 93 f0 0 0 3 2 5 d 9 0 6 11 11 8 b 4 41 e 11 7 21 83 31 c 21 21 a 0 11 0 2 c1 11 11
  //   4 5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
  //   Data ready by /CLK mid-cycle for VDP
  //   Row of 32
  //   Data from memory latched at \CLK
  //   8 Chips Text Color / 2bpp
  //   U48 4-bit DFF with Clear 74LS175 (FG)
  //   U49 4-bit DFF with Clear 74LS175 (BG)
  //   U50 Quad 1-of-2 MUX 74LS157 (FG)
  //   U51 Quad 1-of-2 MUX 74LS157 (BG)
  //   U45 Dual D-FF 74LS74 (Delay/Clocking)
  //   U46 Dual 1-of-4 74LS153 (Palette MUX)
  //   U47 Dual 1-of-4 74LS153 (Palette MUX)
  //   U52 8-bit Register 74LS273 (Color 2/3)
  //   U53 8-bit Register 74LS273 (VDP Latch)
  //   U54 Quad 1-of-2 MUX 74LS157 (Gfx MUX)
  //   U55 Quad 1-of-2 MUX 74LS157 (Gfx MUX)
  //   U56 Triple 3-AND 74LS11 (Color Decode)
  //   U54
  //   U55
endmodule

// DBUS
module PSG (
  input  HSync,
  input  nPHI2,
  input  nWR,
  input  [7:0] DBUS,
  output SND
);

  wire CounterHi_pin1, CounterHi_pin7, CounterHi_pin9, CounterHi_pin15, CounterLo_pin1, CounterLo_pin7,
       FreqLatch_pin2, FreqLatch_pin5, FreqLatch_pin6, FreqLatch_pin9, FreqLatch_pin12, FreqLatch_pin15,
       FreqLatch_pin16, FreqLatch_pin19;

  _74377 #(.ShowInternalStructure("true")) FreqLatch (
    .pin1(nWR), .pin2(FreqLatch_pin2), .pin3(DBUS[0]), .pin4(DBUS[1]), .pin5(FreqLatch_pin5),
    .pin6(FreqLatch_pin6), .pin7(DBUS[2]), .pin8(DBUS[3]), .pin9(FreqLatch_pin9), .pin19(FreqLatch_pin19),
    .pin18(DBUS[7]), .pin17(DBUS[6]), .pin16(FreqLatch_pin16), .pin15(FreqLatch_pin15), .pin14(DBUS[5]),
    .pin13(DBUS[4]), .pin12(FreqLatch_pin12), .pin11(nPHI2));
  _74161 #(.ShowInternalStructure("true")) CounterHi (
    .pin1(CounterHi_pin1), .pin2(HSync), .pin3(FreqLatch_pin12), .pin4(FreqLatch_pin15),
    .pin5(FreqLatch_pin16), .pin6(FreqLatch_pin19), .pin7(CounterHi_pin7), .pin15(CounterHi_pin15),
    .pin10(CounterHi_pin7), .pin9(CounterHi_pin9));  // open: pin14, pin13, pin12, pin11
  _74161 #(.ShowInternalStructure("true")) CounterLo (
    .pin1(CounterLo_pin1), .pin2(HSync), .pin3(FreqLatch_pin2), .pin4(FreqLatch_pin5), .pin5(FreqLatch_pin6),
    .pin6(FreqLatch_pin9), .pin7(CounterLo_pin7), .pin15(CounterHi_pin7), .pin10(CounterLo_pin7),
    .pin9(CounterHi_pin9));  // open: pin14, pin13, pin12, pin11
  not not_1 (CounterHi_pin9, CounterHi_pin15);
  T_Flip_Flop t_ff_1 (.clk(HSync), .T(CounterHi_pin15), .Q(SND));  // open: Qn, preset, reset
  LED led_1 (.in(SND));
  // also tied to VCC on the sheet: {CounterHi_pin1, CounterLo_pin1, CounterLo_pin7}

  // Notes on the sheet:
  //   nWR: initial=0x1
  //   DBUS: initial=0x80
  //   Note: if using 374, NOR nWR with nPHI2
  //   IO address decode
  //   Rising Edge as PHI2 falls
  //   74LS374 ?
  //   15720 Hz
  //   DIV 2
endmodule
